# Fritzing sketch Robo_Seguidor_Linha (saved by Fritzing 1.0.4)
breadboards: 1

parts:
  Arduino1 = Arduino Uno (Rev3)
  M1 = gear-motor
  M2 = gear-motor
  S1 = H-Bridge with L298N
  Componente1 = FC-03 [chip_label=FC-03]
  Componente2 = FC-03 [chip_label=FC-03]
  VCC1 = Battery block 9V [internal_resistance=0.1Ω]

nets:
  N1: Arduino1.D10_PWM/SS, S1.IN1
  N2: Arduino1.D11_PWM/MOSI, S1.IN2
  N3: Arduino1.D12/MISO, S1.IN3
  N4: Arduino1.D13/SCK, S1.IN4
  N5: Arduino1.D5_PWM, Componente1.D0
  N6: Arduino1.D6_PWM, Componente2.D0
  5V: Arduino1.5V, Arduino1.VIN, Componente2.VCC, VCC1.+
  GND: Arduino1.GND, S1.GND, Componente1.GND, Componente2.GND, VCC1.-
  N7: M1.pin_1, S1.M1-01
  N8: M1.pin_2, S1.M1-02
  N9: M2.pin_1, S1.M2-01
  N10: M2.pin_2, S1.M2-02

notes:
  Sketch by Pedro
  Robô Seguidor de Linha
  Código:
  Code

custom parts:
  H-Bridge with L298N: h-bridge
  FC-03: FC-03, LM393 IR Speed Sensor Encoder
